// Logisim project PD0_Rodriguez_Bacelar_David.circ as structural Verilog: 1 circuit, main circuit main
module main (
);

  wire [3:0] A___B, A___B___C, adder_1_out, demultiplexer_1_out0, demultiplexer_2_out0, demultiplexer_2_out1,
       MUESTRA_EL_RESULTADO_EN_POSITIVO, multiplexer_1_out, not_1_out, not_2_out;

  Adder #(.width(4)) adder_1 (.a(4'b0101), .b(4'b0010), .out(adder_1_out));  // open: cin, cout
  assign not_1_out = ~4'b0110;  // NOT_Gate not_1, 4 bits wide
  Demultiplexer #(.width(4), .disabled(0), .enable("false")) demultiplexer_1 (
    .out0(demultiplexer_1_out0), .out1(A___B), .in(adder_1_out), .sel(1'b0));
  Adder #(.width(4)) adder_2 (.a(not_1_out), .b(demultiplexer_1_out0), .out(A___B___C), .cin(1'b1));  // open: cout
  Demultiplexer #(.width(4), .disabled(0), .enable("false")) demultiplexer_2 (
    .out0(demultiplexer_2_out0), .out1(demultiplexer_2_out1), .in(multiplexer_1_out),
    .sel(multiplexer_1_out[3]));
  // Probe on multiplexer_1_out
  Multiplexer #(.width(4), .disabled(0), .enable("false")) multiplexer_1 (
    .in0(A___B___C), .in1(A___B), .out(multiplexer_1_out), .sel(1'b0));
  Hex_Digit_Display hex_digit_display_1 (.value(demultiplexer_2_out0));  // open: dp
  assign not_2_out = ~demultiplexer_2_out1;  // NOT_Gate not_2, 4 bits wide
  Hex_Digit_Display hex_digit_display_2 (.value(MUESTRA_EL_RESULTADO_EN_POSITIVO));  // open: dp
  Adder #(.width(4)) adder_3 (.a(not_2_out), .b(4'b0001), .out(MUESTRA_EL_RESULTADO_EN_POSITIVO));  // open: cin, cout
endmodule
