// Logisim project PD1_Rodriguez_Bacelar_David.circ as structural Verilog: 1 circuit, main circuit main
module main (
);

  wire comparator_1_gt, comparator_2_lt, or_1_out;
  wire [4:0] A___3, B___2____4, not_1_out, Y;

  // Probe on Y
  // Probe on 4'b1111
  // Probe on 4'b1001
  assign not_1_out = ~5'b00100;  // NOT_Gate not_1, 5 bits wide
  // Probe on A___3
  Adder #(.width(5)) adder_1 (.a({5{1'b1}}), .b(5'b00011), .out(A___3));  // open: cin, cout
  // Probe on B___2____4
  Adder #(.width(5)) adder_2 (.a(not_1_out), .b(5'b10010), .out(B___2____4), .cin(1'b1));  // open: cout
  // Probe on 5'b10010
  Comparator #(.width(5), .mode("unsigned")) comparator_1 (
    .a(5'b01111), .b(5'b10011), .gt(comparator_1_gt));  // open: eq, lt
  Comparator #(.width(5), .mode("unsigned")) comparator_2 (
    .a(5'b01001), .b(5'b10100), .lt(comparator_2_lt));  // open: gt, eq
  or or_1 (or_1_out, comparator_1_gt, comparator_2_lt);
  Multiplexer #(.width(5), .disabled(0), .enable("false")) multiplexer_1 (
    .in0(B___2____4), .in1(A___3), .out(Y), .sel(or_1_out));
endmodule
